# Fritzing sketch board (saved by Fritzing 0.9.3b)
circuit board: 5.99418cm x 5.41629cm
breadboards: 1

parts:
  RFM69HCW = Adafruit RFM69HCW Transceiver Radio [part_number="Adafruit #3070 and #3071"]
  R8 = Resistor [tolerance=±5% resistance=470 package=THT]
  LED7 = LED - 3mm [color="Red (633nm)" package="3 mm [THT]"]
  GND = female pin header, 2 pins [form="♀ (female)"]
  VIN = female pin header, 2 pins [form="♀ (female)"]
  BAT- = female pin header, 1 pin [form="♀ (female)"]
  BAT+ = female pin header, 1 pin [form="♀ (female)"]
  ATmega328P = atmega328 [package=dip]
  AVR_ISP_MKII = AVR ISP 6 Pin [package=2x3-ns]
  R1 = Resistor [tolerance=±5% resistance=22k package=THT]
  B1 = Pushbutton [package="[THT]"]
  RESET = Pushbutton [package="[THT]"]
  SENSOR = female pin header, 5 pins [form="♀ (female)"]
  LED8 = LED - 3mm [color="Red (633nm)" package="3 mm [THT]"]
  LED9 = LED - 3mm [color="Red (633nm)" package="3 mm [THT]"]
  LED10 = LED - 3mm [color="Red (633nm)" package="3 mm [THT]"]
  LED11 = LED - 3mm [color="Red (633nm)" package="3 mm [THT]"]
  LED12 = LED - 3mm [color="Red (633nm)" package="3 mm [THT]"]
  R10 = Resistor [tolerance=±5% resistance=470 package=THT]
  R11 = Resistor [tolerance=±5% resistance=470 package=THT]
  R12 = Resistor [tolerance=±5% resistance=470 package=THT]
  R13 = Resistor [tolerance=±5% resistance=470 package=THT]
  R14 = Resistor [tolerance=±5% resistance=470 package=THT]
  TOGGLE_SWITCHES1 = double row male pin header, 12 pins [form="♂ (male)"]

nets:
  N1: RFM69HCW.VIN, TOGGLE_SWITCHES1.pin7
  GND: RFM69HCW.GND, GND.pin1, GND.pin2, BAT-.pin1, ATmega328P.GND, AVR_ISP_MKII.6, B1.Pin_1, B1.Pin_2, RESET.Pin_3, RESET.Pin_4, SENSOR.pin5, TOGGLE_SWITCHES1.pin8, TOGGLE_SWITCHES1.pin9, TOGGLE_SWITCHES1.pin10, TOGGLE_SWITCHES1.pin11, TOGGLE_SWITCHES1.pin12
  N2: RFM69HCW.EN, ATmega328P.D0_(RX)
  N3: RFM69HCW.DIO0, ATmega328P.D2
  N4: RFM69HCW.SCK, ATmega328P.D13, AVR_ISP_MKII.3
  N5: RFM69HCW.MISO, ATmega328P.D12, AVR_ISP_MKII.1
  N6: RFM69HCW.MOSI, ATmega328P.D11_(PWM), AVR_ISP_MKII.4
  N7: RFM69HCW.CS, ATmega328P.D10_(PWM)
  N8: RFM69HCW.RST, ATmega328P.D4
  N9: R8.Pin_0, LED7.cathode
  N10: R8.Pin_1, ATmega328P.A5
  N11: LED7.anode, VIN.pin1, VIN.pin2, BAT+.pin1, ATmega328P.VCC, ATmega328P.AVCC, ATmega328P.AREF, AVR_ISP_MKII.2, R1.Pin_0, LED8.anode, LED9.anode, LED10.anode, LED11.anode, LED12.anode, TOGGLE_SWITCHES1.pin6
  N12: ATmega328P.RESET, AVR_ISP_MKII.5, R1.Pin_1, RESET.Pin_1, RESET.Pin_2
  N13: ATmega328P.D1_(TX), B1.Pin_3, B1.Pin_4
  N14: ATmega328P.D3_(PWM), TOGGLE_SWITCHES1.pin2
  N15: ATmega328P.XLAT1, TOGGLE_SWITCHES1.pin3
  N16: ATmega328P.XLAT2, TOGGLE_SWITCHES1.pin4
  N17: ATmega328P.D5_(PWM), SENSOR.pin1
  N18: ATmega328P.D6_(PWM), SENSOR.pin2
  N19: ATmega328P.D7, SENSOR.pin3
  N20: ATmega328P.D8, SENSOR.pin4
  N21: ATmega328P.D9_(PWM), TOGGLE_SWITCHES1.pin5
  N22: ATmega328P.A0, R10.Pin_1
  N23: ATmega328P.A1, R11.Pin_1
  N24: ATmega328P.A2, R12.Pin_1
  N25: ATmega328P.A3, R13.Pin_1
  N26: ATmega328P.A4, R14.Pin_1
  N27: LED8.cathode, R14.Pin_0
  N28: LED9.cathode, R13.Pin_0
  N29: LED10.cathode, R12.Pin_0
  N30: LED11.cathode, R11.Pin_0
  N31: LED12.cathode, R10.Pin_0

custom parts:
  Adafruit RFM69HCW Transceiver Radio: Sending data over long distances is like magic, and now you can be a magician with this range of powerful and easy-to-use radio modules. Sure, sometimes you want to talk to a computer (a good time to use WiFi) or perhaps communicate with a Phone (choose Bluetooth Low Energy!) but what if you want to send data very far? Most WiFi, Bluetooth, Zigbee and other wireless chipsets use 2.4GHz, which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
