# Fritzing sketch sensor (saved by Fritzing 0.9.3b)
circuit board: 7.5cm x 1.55061cm
breadboards: 1

parts:
  L4 = female pin header, 1 pin [form="♀ (female)"]
  L3 = female pin header, 1 pin [form="♀ (female)"]
  L2 = female pin header, 1 pin [form="♀ (female)"]
  L1 = female pin header, 1 pin [form="♀ (female)"]
  GND = female pin header, 1 pin [form="♀ (female)"]
  SENSOR = female pin header, 5 pins [form="♀ (female)"]

nets:
  N1: L4.pin1, SENSOR.pin1
  N2: L3.pin1, SENSOR.pin2
  N3: L2.pin1, SENSOR.pin3
  N4: L1.pin1, SENSOR.pin4
  N5: GND.pin1, SENSOR.pin5

notes:
  PROJECT WARTHOG
