# Fritzing sketch warthog (saved by Fritzing 0.9.3b)
circuit board: 7.5cm x 1.55061cm
circuit board: 5.99418cm x 5.41629cm
breadboards: 1

parts:
  ATmega328P = atmega328 [package=dip]
  AVR_ISP_MKII = AVR ISP 6 Pin [package=2x3-ns]
  RFM69HCW = Adafruit RFM69HCW Transceiver Radio [part_number="Adafruit #3070 and #3071"]
  R1 = Resistor [tolerance=±5% resistance=22k package=THT]
  RESET = Pushbutton [package="[THT]"]
  SENSOR = female pin header, 5 pins [form="♀ (female)"]
  GND = female pin header, 1 pin [form="♀ (female)"]
  L1 = female pin header, 1 pin [form="♀ (female)"]
  L2 = female pin header, 1 pin [form="♀ (female)"]
  L3 = female pin header, 1 pin [form="♀ (female)"]
  L4 = female pin header, 1 pin [form="♀ (female)"]
  SENSOR_2 = female pin header, 5 pins [form="♀ (female)"]
  R3 = Resistor [tolerance=±5% resistance=470 package=THT]
  R4 = Resistor [tolerance=±5% resistance=470 package=THT]
  R5 = Resistor [tolerance=±5% resistance=470 package=THT]
  R6 = Resistor [tolerance=±5% resistance=470 package=THT]
  R7 = Resistor [tolerance=±5% resistance=470 package=THT]
  LED2 = LED - 3mm [color="Red (633nm)" package="3 mm [THT]"]
  LED3 = LED - 3mm [color="Red (633nm)" package="3 mm [THT]"]
  LED4 = LED - 3mm [color="Red (633nm)" package="3 mm [THT]"]
  LED5 = LED - 3mm [color="Red (633nm)" package="3 mm [THT]"]
  LED6 = LED - 3mm [color="Red (633nm)" package="3 mm [THT]"]
  TOGGLE_SWITCHES = double row male pin header, 12 pins [form="♂ (male)"]
  R2 = Resistor [tolerance=±5% resistance=470 package=THT]
  LED1 = LED - 3mm [color="Red (633nm)" package="3 mm [THT]"]
  BAT+ = female pin header, 1 pin [form="♀ (female)"]
  BAT- = female pin header, 1 pin [form="♀ (female)"]
  VIN = female pin header, 2 pins [form="♀ (female)"]
  GND_2 = female pin header, 2 pins [form="♀ (female)"]
  B1 = Pushbutton [package="[THT]"]

nets:
  N1: ATmega328P.RESET, AVR_ISP_MKII.5, R1.Pin_1, RESET.Pin_1, RESET.Pin_2
  RFM-EN: ATmega328P.D0_(RX), RFM69HCW.EN
  B1: ATmega328P.D1_(TX), B1.Pin_3, B1.Pin_4
  RFM_G0: ATmega328P.D2, RFM69HCW.DIO0
  J2: ATmega328P.D3_(PWM), TOGGLE_SWITCHES.pin2
  RFM-RST: ATmega328P.D4, RFM69HCW.RST
  5V/J6_IN: ATmega328P.VCC, ATmega328P.AVCC, ATmega328P.AREF, AVR_ISP_MKII.2, R1.Pin_0, LED2.anode, LED3.anode, LED4.anode, LED5.anode, LED6.anode, TOGGLE_SWITCHES.pin6, LED1.anode, BAT+.pin1, VIN.pin1, VIN.pin2
  GND: ATmega328P.GND, AVR_ISP_MKII.6, RFM69HCW.GND, RESET.Pin_3, RESET.Pin_4, SENSOR.pin5, TOGGLE_SWITCHES.pin8, TOGGLE_SWITCHES.pin9, TOGGLE_SWITCHES.pin10, TOGGLE_SWITCHES.pin11, TOGGLE_SWITCHES.pin12, BAT-.pin1, GND_2.pin1, GND_2.pin2, B1.Pin_1, B1.Pin_2
  J3: ATmega328P.XLAT1, TOGGLE_SWITCHES.pin3
  J4: ATmega328P.XLAT2, TOGGLE_SWITCHES.pin4
  N2: ATmega328P.D5_(PWM), SENSOR.pin1
  N3: ATmega328P.D6_(PWM), SENSOR.pin2
  N4: ATmega328P.D7, SENSOR.pin3
  N5: ATmega328P.D8, SENSOR.pin4
  J5: ATmega328P.D9_(PWM), TOGGLE_SWITCHES.pin5
  CS: ATmega328P.D10_(PWM), RFM69HCW.CS
  MOSI: ATmega328P.D11_(PWM), AVR_ISP_MKII.4, RFM69HCW.MOSI
  MISO: ATmega328P.D12, AVR_ISP_MKII.1, RFM69HCW.MISO
  SCK: ATmega328P.D13, AVR_ISP_MKII.3, RFM69HCW.SCK
  N6: ATmega328P.A0, R7.Pin_1
  N7: ATmega328P.A1, R6.Pin_1
  N8: ATmega328P.A2, R5.Pin_1
  N9: ATmega328P.A3, R4.Pin_1
  N10: ATmega328P.A4, R3.Pin_1
  N11: ATmega328P.A5, R2.Pin_1
  J6_OUT: RFM69HCW.VIN, TOGGLE_SWITCHES.pin7
  N12: GND.pin1, SENSOR_2.pin5
  N13: L1.pin1, SENSOR_2.pin4
  N14: L2.pin1, SENSOR_2.pin3
  N15: L3.pin1, SENSOR_2.pin2
  N16: L4.pin1, SENSOR_2.pin1
  N17: R3.Pin_0, LED2.cathode
  N18: R4.Pin_0, LED3.cathode
  N19: R5.Pin_0, LED4.cathode
  N20: R6.Pin_0, LED5.cathode
  N21: R7.Pin_0, LED6.cathode
  N22: R2.Pin_0, LED1.cathode

notes:
  Dog bowl
  PROJECT WARTHOG

custom parts:
  Adafruit RFM69HCW Transceiver Radio: Sending data over long distances is like magic, and now you can be a magician with this range of powerful and easy-to-use radio modules. Sure, sometimes you want to talk to a computer (a good time to use WiFi) or perhaps communicate with a Phone (choose Bluetooth Low Energy!) but what if you want to send data very far? Most WiFi, Bluetooth, Zigbee and other wireless chipsets use 2.4GHz, which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
